// Logisim project Processor.circ as structural Verilog: 8 circuits, main circuit ALU
module main (
);

  wire CLK, controlunit_1_alusrc, controlunit_1_memtoreg, controlunit_1_memwrite, controlunit_1_pcsrc,
       controlunit_1_r2orimmtoreg, controlunit_1_regwrite, RESET;
  wire [0:0] controlunit_1_regsrc;
  wire [1:0] controlunit_1_immsrc, controlunit_1_regsrc_2;
  wire [2:0] controlunit_1_alucontrol;
  wire [3:0] aluw_flags_1_aluflags, multiplexer_2_out, multiplexer_3_out, rom_1_data_2;
  wire [23:0] adder_1_out, adder_2_out, multiplexer_1_out, multiplexer_4_out, PC_q;
  wire [31:0] aluw_flags_1_result, bit_extender_1_out, extender_1_out, multiplexer_5_out, multiplexer_6_out,
       ram_1_data, REG_rd1, REG_rd2, rom_1_data, shifter_1_out;
  wire [31:24] multiplexer_4_out_2;

  Clock clock_1 (.out(CLK));
  Button button_1 (.out(RESET));
  Multiplexer #(.width(24), .enable("false")) multiplexer_1 (
    .in0(multiplexer_4_out), .in1(adder_1_out), .out(multiplexer_1_out), .sel(controlunit_1_pcsrc));
  Register #(.width(24)) PC (.D(multiplexer_1_out), .Q(PC_q), .clk(CLK), .clr(RESET));  // open: en
  Adder #(.width(24)) adder_1 (.a(PC_q), .b(24'h1), .out(adder_1_out));  // open: cin, cout
  ROM #(.addrWidth(24), .dataWidth(32)) rom_1 (
    .addr(PC_q), .data({rom_1_data[31:16], rom_1_data_2, rom_1_data[11:0]}));  // open: sel
  Adder #(.width(24)) adder_2 (.a(adder_1_out), .b(24'h1), .out(adder_2_out));  // open: cin, cout
  assign bit_extender_1_out = {{8{1'b0}}, adder_2_out};  // Bit_Extender bit_extender_1
  ControlUnit controlunit_1 (
    .Cond(rom_1_data[31:28]), .Opt(rom_1_data[27:26]), .Funct(rom_1_data[25:20]), .Rd(rom_1_data_2),
    .MemtoReg(controlunit_1_memtoreg), .MemWrite(controlunit_1_memwrite),
    .ALUControl(controlunit_1_alucontrol), .ALUSrc(controlunit_1_alusrc), .ImmSrc(controlunit_1_immsrc),
    .RegWrite(controlunit_1_regwrite), .RegSrc({controlunit_1_regsrc_2, controlunit_1_regsrc[0]}),
    .Flags(aluw_flags_1_aluflags), .R2orImmtoReg(controlunit_1_r2orimmtoreg), .Shift(rom_1_data[6:4]),
    .CLK(CLK), .PCSrc(controlunit_1_pcsrc));
  Multiplexer #(.select(2), .width(4), .enable("false")) multiplexer_2 (
    .in0(rom_1_data[19:16]), .in1(4'b1111), .in2(rom_1_data[3:0]), .out(multiplexer_2_out),
    .sel(controlunit_1_regsrc_2));  // open: in3
  Multiplexer #(.width(4), .enable("false")) multiplexer_3 (
    .in0(rom_1_data[3:0]), .in1(rom_1_data_2), .out(multiplexer_3_out), .sel(controlunit_1_regsrc[0]));
  RegisterField REG (
    .A1(multiplexer_2_out), .A2(multiplexer_3_out), .A3(rom_1_data_2), .WE3(controlunit_1_regwrite),
    .WD3({multiplexer_4_out_2, multiplexer_4_out}), .RD1(REG_rd1), .RD2(REG_rd2), .CLK(CLK),
    .R15(bit_extender_1_out), .Reset(RESET));
  Extender extender_1 (
    .In({rom_1_data[23:16], rom_1_data_2, rom_1_data[11:0]}), .Out(extender_1_out),
    .ImmSrc(controlunit_1_immsrc));
  Shifter shifter_1 (.ShiftCtrl(rom_1_data[6:5]), .A(REG_rd2), .Out(shifter_1_out), .Width(rom_1_data[11:7]));
  Multiplexer #(.width(32), .enable("false")) multiplexer_4 (
    .in0(multiplexer_6_out), .in1(multiplexer_5_out), .out({multiplexer_4_out_2, multiplexer_4_out}),
    .sel(controlunit_1_r2orimmtoreg));
  Multiplexer #(.width(32), .enable("false")) multiplexer_5 (
    .in0(shifter_1_out), .in1(extender_1_out), .out(multiplexer_5_out), .sel(controlunit_1_alusrc));
  ALUw_Flags aluw_flags_1 (
    .B(multiplexer_5_out), .A(REG_rd1), .Result(aluw_flags_1_result), .ALUFlags(aluw_flags_1_aluflags),
    .ALUControl(controlunit_1_alucontrol));
  RAM #(.addrWidth(24), .dataWidth(32), .bus("separate")) ram_1 (
    .addr(aluw_flags_1_result[23:0]), .din(REG_rd2), .data(ram_1_data), .str(controlunit_1_memwrite),
    .clk(CLK), .clr(RESET));  // open: sel, ld
  Multiplexer #(.width(32), .enable("false")) multiplexer_6 (
    .in0(aluw_flags_1_result), .in1(ram_1_data), .out(multiplexer_6_out), .sel(controlunit_1_memtoreg));

  // Notes on the sheet:
  //   PCPlus1
  //   contents of rom_1 (hex, n*v repeats v):
  //   e3a01006 e3a02005 e3a04001 e0813002 e1a03083 e0533004 e2855001 1afffffc
  //   PCPlus2
endmodule

module ALU (
  input  [1:0] ALUControl,
  input  [31:0] B,
  input  [31:0] A,
  output [31:0] Result
);

  wire [31:0] adder_1_out, and_1_out, multiplexer_1_out, not_1_out, or_1_out;

  Multiplexer #(.width(32), .enable("false")) multiplexer_1 (
    .in0(B), .in1(not_1_out), .out(multiplexer_1_out), .sel(ALUControl[0]));
  assign not_1_out = ~B;  // NOT_Gate not_1, 32 bits wide
  Adder #(.width(32)) adder_1 (.a(multiplexer_1_out), .b(A), .out(adder_1_out), .cin(ALUControl[0]));  // open: cout
  assign and_1_out = B & A;  // AND_Gate and_1, 32 bits wide
  assign or_1_out = B | A;  // OR_Gate or_1, 32 bits wide
  Multiplexer #(.select(2), .width(32), .enable("false")) multiplexer_2 (
    .in0(adder_1_out), .in1(adder_1_out), .in2(and_1_out), .in3(or_1_out), .out(Result), .sel(ALUControl));
endmodule

module RegisterField (
  input  CLK,
  input  Reset,
  input  [3:0] A1,
  input  [3:0] A2,
  input  [3:0] A3,
  input  WE3,
  input  [31:0] WD3,
  input  [31:0] R15,
  output [31:0] RD1,
  output [31:0] RD2
);

  wire demultiplexer_1_out0, demultiplexer_1_out1, demultiplexer_1_out2, demultiplexer_1_out3,
       demultiplexer_1_out4, demultiplexer_1_out5, demultiplexer_1_out6, demultiplexer_1_out7,
       demultiplexer_1_out8, demultiplexer_1_out9, demultiplexer_1_out10, demultiplexer_1_out11,
       demultiplexer_1_out12, demultiplexer_1_out13, demultiplexer_1_out14;
  wire [31:0] r0_q, r1_q, r2_q, r3_q, r4_q, r5_q, r6_q, r7_q, r8_q, r9_q, r10_q, r11_q, r12_q, r13_q, r14_q;

  Demultiplexer #(.select(4), .enable("false")) demultiplexer_1 (
    .out0(demultiplexer_1_out0), .out1(demultiplexer_1_out1), .out2(demultiplexer_1_out2),
    .out3(demultiplexer_1_out3), .out4(demultiplexer_1_out4), .out5(demultiplexer_1_out5),
    .out6(demultiplexer_1_out6), .out7(demultiplexer_1_out7), .out8(demultiplexer_1_out8),
    .out9(demultiplexer_1_out9), .out10(demultiplexer_1_out10), .out11(demultiplexer_1_out11),
    .out12(demultiplexer_1_out12), .out13(demultiplexer_1_out13), .out14(demultiplexer_1_out14), .in(WE3),
    .sel(A3));  // open: out15
  Register #(.width(32)) r0 (.D(WD3), .en(demultiplexer_1_out0), .Q(r0_q), .clk(CLK), .clr(Reset));
  Register #(.width(32)) r4 (.D(WD3), .en(demultiplexer_1_out4), .Q(r4_q), .clk(CLK), .clr(Reset));
  Register #(.width(32)) r8 (.D(WD3), .en(demultiplexer_1_out8), .Q(r8_q), .clk(CLK), .clr(Reset));
  Register #(.width(32)) r12 (.D(WD3), .en(demultiplexer_1_out12), .Q(r12_q), .clk(CLK), .clr(Reset));
  Register #(.width(32)) r1 (.D(WD3), .en(demultiplexer_1_out1), .Q(r1_q), .clk(CLK), .clr(Reset));
  Register #(.width(32)) r5 (.D(WD3), .en(demultiplexer_1_out5), .Q(r5_q), .clk(CLK), .clr(Reset));
  Register #(.width(32)) r9 (.D(WD3), .en(demultiplexer_1_out9), .Q(r9_q), .clk(CLK), .clr(Reset));
  Register #(.width(32)) r13 (.D(WD3), .en(demultiplexer_1_out13), .Q(r13_q), .clk(CLK), .clr(Reset));
  Register #(.width(32)) r2 (.D(WD3), .en(demultiplexer_1_out2), .Q(r2_q), .clk(CLK), .clr(Reset));
  Register #(.width(32)) r6 (.D(WD3), .en(demultiplexer_1_out6), .Q(r6_q), .clk(CLK), .clr(Reset));
  Register #(.width(32)) r10 (.D(WD3), .en(demultiplexer_1_out10), .Q(r10_q), .clk(CLK), .clr(Reset));
  Register #(.width(32)) r14 (.D(WD3), .en(demultiplexer_1_out14), .Q(r14_q), .clk(CLK), .clr(Reset));
  Register #(.width(32)) r3 (.D(WD3), .en(demultiplexer_1_out3), .Q(r3_q), .clk(CLK), .clr(Reset));
  Register #(.width(32)) r7 (.D(WD3), .en(demultiplexer_1_out7), .Q(r7_q), .clk(CLK), .clr(Reset));
  Register #(.width(32)) r11 (.D(WD3), .en(demultiplexer_1_out11), .Q(r11_q), .clk(CLK), .clr(Reset));
  Multiplexer #(.select(4), .width(32), .enable("false")) multiplexer_1 (
    .in0(r0_q), .in1(r1_q), .in2(r2_q), .in3(r3_q), .in4(r4_q), .in5(r5_q), .in6(r6_q), .in7(r7_q),
    .in8(r8_q), .in9(r9_q), .in10(r10_q), .in11(r11_q), .in12(r12_q), .in13(r13_q), .in14(r14_q), .in15(R15),
    .out(RD1), .sel(A1));
  Multiplexer #(.select(4), .width(32), .enable("false")) multiplexer_2 (
    .in0(r0_q), .in1(r1_q), .in2(r2_q), .in3(r3_q), .in4(r4_q), .in5(r5_q), .in6(r6_q), .in7(r7_q),
    .in8(r8_q), .in9(r9_q), .in10(r10_q), .in11(r11_q), .in12(r12_q), .in13(r13_q), .in14(r14_q), .in15(R15),
    .out(RD2), .sel(A2));
endmodule

module ControlUnit (
  input  [1:0] Opt,
  input  CLK,
  input  [3:0] Cond,
  input  [2:0] Shift,
  input  [3:0] Rd,
  input  [3:0] Flags,
  input  [5:0] Funct,
  output MemtoReg,
  output PCSrc,
  output [2:0] RegSrc,
  output [2:0] ALUControl,
  output R2orImmtoReg,
  output ALUSrc,
  output [1:0] ImmSrc,
  output MemWrite,
  output RegWrite
);

  wire ALUOp, and_3_out, and_4_out, and_5_out, and_6_out, and_8_out, and_12_out, and_14_out, and_15_out,
       and_16_out, and_17_out, and_19_out, and_20_out, and_21_out, and_22_out, and_23_out, and_24_out,
       and_25_out, and_28_out, and_29_out, and_30_out, and_31_out, and_32_out, and_33_out, and_34_out,
       and_35_out, CondMet, DiscardResult, not_1_out, not_2_out, not_3_out, not_4_out, not_5_out, not_6_out,
       not_7_out, not_8_out, not_9_out, not_10_out, not_11_out, not_12_out, not_13_out, not_14_out,
       not_15_out, not_16_out, not_17_out, not_18_out, not_19_out, not_20_out, not_21_out, not_22_out,
       not_23_out, not_24_out, not_26_out, not_27_out, not_28_out, or_2_out, or_3_out, or_4_out, or_5_out,
       or_6_out, or_7_out, or_8_out, xnor_1_out;
  wire [0:0] and_18_out;
  wire [1:0] FlagW, multiplexer_8_out, VC_q, ZN_q;
  wire [2:0] multiplexer_1_out, multiplexer_2_out, multiplexer_3_out, multiplexer_4_out;

  not not_1 (not_1_out, Funct[3]);
  not not_2 (not_2_out, Opt[0]);
  not not_3 (not_3_out, Opt[1]);
  and and_1 (DiscardResult, not_1_out, Funct[4]);
  and and_2 (ALUOp, not_2_out, not_3_out);
  Multiplexer #(.select(2), .width(3), .enable("false")) multiplexer_1 (
    .in0(3'b100), .in1(3'b101), .in2(3'b110), .out(multiplexer_1_out), .sel(Shift[2:1]));  // open: in3
  Multiplexer #(.width(3), .enable("false")) multiplexer_2 (
    .in0(multiplexer_1_out), .in1(3'b100), .out(multiplexer_2_out), .sel(Funct[5]));
  Multiplexer #(.select(4), .width(3), .enable("false")) multiplexer_3 (
    .in0(3'b010), .in2(3'b001), .in4(3'b000), .in8(3'b010), .in10(3'b001), .in11(3'b000), .in12(3'b011),
    .in13(multiplexer_2_out), .in15(3'b111), .out(multiplexer_3_out), .sel(Funct[4:1]));  // open: in1, in3, in5, in6, in7, in9, in14
  Multiplexer #(.width(3), .enable("false")) multiplexer_4 (
    .in0(3'b001), .in1(3'b000), .out(multiplexer_4_out), .sel(Funct[3]));
  and and_3 (and_3_out, RegSrc[2], not_4_out);
  not not_4 (not_4_out, Funct[5]);
  Multiplexer #(.select(2), .width(3), .enable("false")) multiplexer_5 (
    .in0(multiplexer_3_out), .in1(multiplexer_4_out), .in2(3'b000), .out(ALUControl), .sel(Opt));  // open: in3
  not not_5 (not_5_out, Opt[0]);
  not not_6 (not_6_out, Opt[1]);
  not not_7 (not_7_out, Funct[2]);
  Multiplexer #(.width(2), .enable("false")) multiplexer_6 (.in0(Opt), .in1(2'b11), .out(ImmSrc), .sel(and_3_out));
  and and_4 (and_4_out, not_5_out, not_6_out);
  and and_5 (and_5_out, Funct[1], not_7_out, Funct[3], Funct[4]);
  not not_8 (not_8_out, Funct[2]);
  and and_6 (and_6_out, Funct[1], not_8_out, Funct[3], Funct[4]);
  not not_9 (not_9_out, Opt[0]);
  not not_10 (not_10_out, Opt[1]);
  and and_7 (RegSrc[2], ALUOp, and_6_out);
  not not_11 (not_11_out, Opt[1]);
  and and_8 (and_8_out, not_9_out, not_10_out);
  and and_9 (RegSrc[0], and_8_out, Funct[5]);
  and and_10 (RegSrc[1], not_12_out, Opt[1]);
  not not_12 (not_12_out, Opt[0]);
  and and_11 (R2orImmtoReg, and_4_out, and_5_out, Funct[5]);
  not not_13 (not_13_out, Shift[0]);
  and and_12 (and_12_out, Opt[0], ~Opt[1]);  // AND_Gate
  and and_13 (MemtoReg, Funct[0], and_14_out);
  and and_14 (and_14_out, Opt[0], not_11_out);
  and and_15 (and_15_out, not_13_out, RegSrc[2]);
  and and_16 (and_16_out, ~ALUControl[0], ~ALUControl[1], ~ALUControl[2]);  // AND_Gate
  and and_17 (and_17_out, ALUControl[0], ~ALUControl[1], ~ALUControl[2]);  // AND_Gate
  or or_1 (ALUSrc, Funct[5], and_15_out, and_12_out);
  and and_18 (and_18_out[0], Funct[0], or_2_out);
  or or_2 (or_2_out, and_16_out, and_17_out);
  Multiplexer #(.width(2), .enable("false")) multiplexer_7 (
    .in0(2'b00), .in1({Funct[0], and_18_out[0]}), .out(FlagW), .sel(ALUOp));
  Multiplexer #(.width(2), .enable("false")) multiplexer_8 (
    .in0(2'b00), .in1(FlagW), .out(multiplexer_8_out), .sel(CondMet));
  Register #(.width(2)) VC (.D({Flags[0], Flags[1]}), .en(multiplexer_8_out[1]), .Q(VC_q), .clk(CLK));  // open: clr
  not not_14 (not_14_out, VC_q[0]);
  not not_15 (not_15_out, VC_q[1]);
  not not_16 (not_16_out, Opt[1]);
  not not_17 (not_17_out, Opt[0]);
  and and_19 (and_19_out, not_17_out, not_18_out);
  not not_18 (not_18_out, Opt[1]);
  and and_20 (and_20_out, Opt[0], not_19_out);
  not not_19 (not_19_out, Opt[1]);
  Register #(.width(2)) ZN (.D({Flags[2], Flags[3]}), .en(multiplexer_8_out[0]), .Q(ZN_q), .clk(CLK));  // open: clr
  not not_20 (not_20_out, ZN_q[0]);
  not not_21 (not_21_out, ZN_q[1]);
  not not_22 (not_22_out, Funct[0]);
  and and_21 (and_21_out, Opt[0], not_16_out);
  and and_22 (and_22_out, and_19_out, not_23_out);
  not not_23 (not_23_out, DiscardResult);
  and and_23 (and_23_out, Funct[0], and_20_out);
  and and_24 (and_24_out, VC_q[0], not_21_out);
  and and_25 (and_25_out, not_22_out, and_21_out);
  or or_3 (or_3_out, and_22_out, and_23_out);
  or or_4 (or_4_out, not_14_out, ZN_q[1]);
  xnor xnor_1 (xnor_1_out, ZN_q[0], VC_q[1]);
  and and_26 (MemWrite, and_25_out, CondMet);
  and and_27 (RegWrite, CondMet, or_3_out);
  and and_28 (and_28_out, Rd[0], Rd[1], Rd[2], Rd[3]);
  and and_29 (and_29_out, xnor_1_out, not_21_out);
  and and_30 (and_30_out, and_28_out, RegWrite);
  and and_31 (and_31_out, ~Opt[0], Opt[1]);  // AND_Gate
  not not_24 (not_24_out, xnor_1_out);
  or or_5 (or_5_out, not_24_out, ZN_q[1]);
  or or_6 (or_6_out, and_30_out, and_31_out);
  Multiplexer #(.select(4), .enable("false")) multiplexer_9 (
    .in0(ZN_q[1]), .in1(not_21_out), .in2(VC_q[0]), .in3(not_14_out), .in4(ZN_q[0]), .in5(not_20_out),
    .in6(VC_q[1]), .in7(not_15_out), .in8(and_24_out), .in9(or_4_out), .in10(xnor_1_out), .in11(not_24_out),
    .in12(and_29_out), .in13(or_5_out), .in14(1'b1), .out(CondMet), .sel(Cond));  // open: in15
  and and_32 (and_32_out, or_6_out, CondMet);
  not not_25 (PCSrc, and_32_out);
  and and_33 (and_33_out, Rd[0], Rd[1], Rd[2], Rd[3]);
  not not_26 (not_26_out, CondMet);
  not not_27 (not_27_out, Opt[0]);
  and and_34 (and_34_out, not_27_out, not_28_out);
  not not_28 (not_28_out, and_33_out);
  or or_7 (or_7_out, not_26_out, and_34_out);
  and and_35 (and_35_out, Opt[0], Opt[1]);
  or or_8 (or_8_out, or_7_out, and_35_out);

  // Other names for the same wires on the sheet: L = Funct[0]; S = Funct[0]; C = Flags[1]; V = Flags[0]; N = Flags[3];
  //   Z = Flags[2]; CMD[3:0] = Funct[4:1]; W = Funct[1]; B = Funct[2]; U = Funct[3]; P = Funct[4]; I = Funct[5];
  //   IsShift = RegSrc[2]

  // Notes on the sheet:
  //   Add
  //   ALU only supports selected functions
  //   ignored by me
  //   ignored by me
  //   ignored by me
  //   AND
  //   SUB
  //   OR
  //   0 = Immediate offset, 1 = Register
  //   0 = Subtract from base, 1 = add
  //   0 = Store, 1 = Load
  //   Represents if arith. command should discard the result (1) or save it (0). Relevant for the cmp and tst commands. 
  //   LSR
  //   LSL
  //   0 = discard flags, 1 = set flags on arith. command
  //   NOT
  //   ASR
  //   Is the current op arithemtic, are we doing a shift and are using the imm (mov)?
  //   00: Zero-Extend Imm8 for Arith-Logic
  //   01: Zero-Extend Imm12 for ldr
  //   10: Sign-Extend imm22 for branch
  //   11: Zero-Extend Shamt5 for shift
  //   Signazlizes if the current operant is a shift command.
  //   RegSrc: XX Y
  //   01 if branch
  //   10 if shift
  //   00 else
  //   Add or sub performed?
  //   1 if str
  //   MemToReg = L AND OPT == 01
  //   0 if arith. command without Imm.
  //   Decoder
  //   Conditional Logik
  //   MemWrite = opt == 01 AND !L AND CondMet
  //   RegWrite = CondMet AND (( opt == 00 AND ! DiscardResult) OR (opt == 01 AND L))
  //   Signalized if condition evaluated to true
  //   PCSrc = ! condMet OR (!opt0 AND ! (RD == 15)) OR (opt0 AND opt1)
endmodule

module Extender (
  input  [1:0] ImmSrc,
  input  [23:0] In,
  output [31:0] Out
);

  wire [31:0] bit_extender_1_out, bit_extender_2_out, bit_extender_3_out, bit_extender_4_out;

  assign bit_extender_1_out = {{24{1'b0}}, In[7:0]};  // Bit_Extender bit_extender_1
  assign bit_extender_2_out = {{20{1'b0}}, In[11:0]};  // Bit_Extender bit_extender_2
  assign bit_extender_3_out = {{8{In[23]}}, In};  // Bit_Extender bit_extender_3
  assign bit_extender_4_out = {{27{1'b0}}, In[11:7]};  // Bit_Extender bit_extender_4
  Multiplexer #(.select(2), .width(32), .enable("false")) multiplexer_1 (
    .in0(bit_extender_1_out), .in1(bit_extender_2_out), .in2(bit_extender_3_out), .in3(bit_extender_4_out),
    .out(Out), .sel(ImmSrc));

  // Notes on the sheet:
  //   01: Zero-Extend Imm12 for ldr
  //   10: Sign-Extend imm22 for branch
  //   11: Zero-Extend Shamt5 for shifts
  //   00: Zero-Extend Imm8 for Arith-Logic
endmodule

module ALUw_Flags (
  input  [2:0] ALUControl,
  input  [31:0] B,
  input  [31:0] A,
  output [31:0] Result,
  output [3:0] ALUFlags
);

  wire adder_1_cout, not_2_out, not_3_out, Sum31, xor_1_out, xor_2_out, xor_3_out;
  wire [30:0] adder_1_out;
  wire [31:0] and_1_out, multiplexer_1_out, negator_1_out, not_1_out, or_1_out, shifter_1_out, shifter_2_out,
       shifter_3_out;

  Multiplexer #(.width(32), .enable("false")) multiplexer_1 (
    .in0(B), .in1(not_1_out), .out(multiplexer_1_out), .sel(ALUControl[0]));
  assign not_1_out = ~B;  // NOT_Gate not_1, 32 bits wide
  not not_2 (not_2_out, ALUControl[1]);
  xor xor_1 (xor_1_out, B[31], A[31]);
  xor xor_2 (xor_2_out, xor_1_out, ALUControl[0]);
  xor xor_3 (xor_3_out, A[31], Sum31);
  Shifter_part #(.width(32)) shifter_1 (.in(A), .\dist (B[4:0]), .out(shifter_1_out));
  Shifter_part #(.width(32), .shift("lr")) shifter_2 (.in(A), .\dist (B[4:0]), .out(shifter_2_out));
  Shifter_part #(.width(32), .shift("ar")) shifter_3 (.in(A), .\dist (B[4:0]), .out(shifter_3_out));
  Negator #(.width(32)) negator_1 (.in(A), .out(negator_1_out));
  not not_3 (not_3_out, xor_2_out);
  Adder #(.width(32)) adder_1 (
    .a(multiplexer_1_out), .b(A), .out({Sum31, adder_1_out}), .cin(ALUControl[0]), .cout(adder_1_cout));
  assign and_1_out = B & A;  // AND_Gate and_1, 32 bits wide
  assign or_1_out = B | A;  // OR_Gate or_1, 32 bits wide
  and and_2 (ALUFlags[1], adder_1_cout, not_2_out);
  and and_3 (ALUFlags[0], not_2_out, not_3_out, xor_3_out);
  Multiplexer #(.select(3), .width(32), .enable("false")) multiplexer_2 (
    .in0({Sum31, adder_1_out}), .in1({Sum31, adder_1_out}), .in2(and_1_out), .in3(or_1_out),
    .in4(shifter_1_out), .in5(shifter_2_out), .in6(shifter_3_out), .in7(negator_1_out),
    .out({ALUFlags[3], Result[30:0]}), .sel(ALUControl));
  Comparator #(.width(32)) comparator_1 (
    .a({ALUFlags[3], Result[30:0]}), .b({32{1'b0}}), .eq(ALUFlags[2]));  // open: gt, lt

  assign Result[31] = ALUFlags[3];

  // Notes on the sheet:
  //   ALUControl1
  //   ALUControl0
  //   3 Input XNOR wegen Bug in XNOR
  //   Carry
  //   Overflow
  //   Zero
  //   Negative
endmodule

module Shifter (
  input  [1:0] ShiftCtrl,
  input  [4:0] Width,
  input  [31:0] A,
  output [31:0] Out
);

  wire [31:0] shifter_1_out, shifter_2_out, shifter_3_out, shifter_4_out;

  Shifter_part #(.width(32)) shifter_1 (.in(A), .\dist (Width), .out(shifter_1_out));
  Shifter_part #(.width(32), .shift("lr")) shifter_2 (.in(A), .\dist (Width), .out(shifter_2_out));
  Shifter_part #(.width(32), .shift("ar")) shifter_3 (.in(A), .\dist (Width), .out(shifter_3_out));
  Shifter_part #(.width(32), .shift("rr")) shifter_4 (.in(A), .\dist (Width), .out(shifter_4_out));
  Multiplexer #(.select(2), .width(32), .enable("false")) multiplexer_1 (
    .in0(shifter_1_out), .in1(shifter_2_out), .in2(shifter_3_out), .in3(shifter_4_out), .out(Out),
    .sel(ShiftCtrl));
endmodule

module PCSrc (
  input  condMet,
  input  opt0,
  input  opt1,
  input  RD15,
  output PCSrc
);

  wire and_1_out, and_2_out, not_1_out, not_2_out, not_3_out, or_1_out;

  not not_1 (not_1_out, condMet);
  not not_2 (not_2_out, opt0);
  and and_1 (and_1_out, not_2_out, not_3_out);
  not not_3 (not_3_out, RD15);
  or or_1 (or_1_out, not_1_out, and_1_out);
  and and_2 (and_2_out, opt0, opt1);
  or or_2 (PCSrc, or_1_out, and_2_out);
endmodule
