// Logisim project Spielwiese.circ as structural Verilog: 1 circuit, main circuit main
module main (
);

  wire clock_1_out, comparator_1_eq, comparator_1_gt, not_1_out, or_1_out;
  wire [7:0] adder_1_out, counter_1_q, multiplexer_1_out, register_1_q;

  Counter counter_1 (
    .load(or_1_out), .D({8{1'b0}}), .count(not_1_out), .Q(counter_1_q), .clk(clock_1_out));  // open: carry, clr
  not not_1 (not_1_out, or_1_out);
  Clock clock_1 (.out(clock_1_out));
  Adder adder_1 (.a(counter_1_q), .b({8{1'b0}}), .out(adder_1_out));  // open: cin, cout
  Register register_1 (.D(adder_1_out), .Q(register_1_q), .clk(clock_1_out));  // open: en, clr
  Multiplexer #(.width(8), .enable("false")) multiplexer_1 (
    .in0(adder_1_out), .in1(register_1_q), .out(multiplexer_1_out), .sel(1'b0));
  Comparator comparator_1 (.a(multiplexer_1_out), .b(8'h8), .gt(comparator_1_gt), .eq(comparator_1_eq));  // open: lt
  LED led_1 (.in(multiplexer_1_out[0]));
  LED led_2 (.in(multiplexer_1_out[1]));
  LED led_3 (.in(multiplexer_1_out[2]));
  LED led_4 (.in(multiplexer_1_out[3]));
  LED led_5 (.in(multiplexer_1_out[4]));
  LED led_6 (.in(multiplexer_1_out[5]));
  LED led_7 (.in(multiplexer_1_out[6]));
  LED led_8 (.in(multiplexer_1_out[7]));
  or or_1 (or_1_out, comparator_1_gt, comparator_1_eq);
endmodule
